# Fritzing sketch sketch (saved by Fritzing 0.9.3b)
breadboards: 1

parts:
  U2 = LIPO-2000mAh [package=lipo-2000]
  U3 = V_REG_LD1117VXX [package=78xxl]
  U4 = ESP8266 WiFi Module [part_number=ESP8266]
  U6 = SWITCH_SPDT [package=kps-1290]
  U7 = SWITCH_SPDT [package=kps-1290]
  Part1 = Adafruit Si7021 Temp Humidity [part_number="Adafruit #3251"]
  C1 = Electrolytic Capacitor [capacitance=22µF voltage=0.1kV package="0405 [SMD, electrolytic]"]
  S3 = Momentary Switch [package=ksa_sealed_tac_switch]
  S4 = Momentary Switch [package=ksa_sealed_tac_switch]
  Part2 = Power Cell LiPo Charger/Booster

nets:
  N1: U2.+, U3.IN, Part2.VCC
  GND: U2.-, U3.GND, U4.GND, U4.GPIO_15, U6.P, U6.S, Part1.VIN, C1.-, S3.2, S4.2, Part2.GND
  N2: U3.OUT, U7.S
  VCC: U4.VCC, U4.GPIO_2, U4.CH_PD, U7.P, Part1.+3V3, C1.+
  N3: U4.GPIO_0, U6.O
  N4: U4.GPIO_4, S4.1
  N5: U4.GPIO_16, U4.REST, S3.3
  N6: U4.GPIO_12, Part1.SCL
  N7: U4.GPIO_13, Part1.SDA

custom parts:
  Adafruit Si7021 Temp Humidity: It's summer and you're sweating and your hair's all frizzy and all you really want to know is why the weatherman said this morning that today's relative humidity would max out at a perfectly reasonable 42% when it feels more like 77%. Enter the Si7021 Temperature + Humidity Sensor - the best way to prove the weatherman wrong! This lovely sensor for Silicon labs has ± 3% relative humidity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
